# Fritzing sketch IotProj (saved by Fritzing 0.9.5d)
breadboards: 1

parts:
  U1 = ESP8266 NodeMCU LoLin module
  DHT1 = DHT11 Humitidy and Temperature Sensor
  FC-1 = Sound Sensor

nets:
  N1: U1.D3, DHT1.DATA
  3V3: U1.3V3, FC-1.VCC
  GND: U1.GND, DHT1.GND, FC-1.GND
  VIN: U1.Vin, DHT1.VDD
  N2: U1.A0, FC-1.OUT

custom parts:
  ESP8266 NodeMCU LoLin module: ESP8266 based NodeMCU
  DHT11 Humitidy and Temperature Sensor: DHT11 Humidity and Temperature Sensor
